# Fritzing sketch Schematic (saved by Fritzing 0.9.4)
breadboards: 1

parts:
  Part2 = Arduino Mega 2560 (Rev3)
  LCM1602_IIC1 = LCM1602 IIC [part_number="LCM1602 IIC" chip_label="LCM1602 IIC" package="DIP (Dual Inline) [THT]"]
  LCD1 = LCD screen
  Keypad4x1 = Keypad Membran 4x4
  Part3 = Passive Buzzer
  U1 = 2-Channel 5v Relay Shield [package=relay-2ch5v10a]
  S1 = Round Pushbutton
  S2 = Round Pushbutton
  ZS-042_RTC1 = ZS-042 RTC Module
  Part4 = RDM6300-ANT
  125_kHz_RFID_module1 = RDM6300

nets:
  N1: Part2.A0, S1.leg0
  N2: Part2.A1, S2.leg0
  N3: Part2.SCL, LCM1602_IIC1.SCL, ZS-042_RTC1.SCL
  N4: Part2.SDA, LCM1602_IIC1.SDA, ZS-042_RTC1.SDA
  GND: Part2.GND, Part2.D53, LCM1602_IIC1.GND, Part3.GND, U1.GND, S1.leg1, S2.leg1, ZS-042_RTC1.GND, 125_kHz_RFID_module1.TX, 125_kHz_RFID_module1.GND
  N5: Part2.D11_PWM, Part3.S
  N6: Part2.D10_PWM, U1.IN1
  N7: Part2.D9_PWM, Keypad4x1.Pin1
  N8: Part2.D8_PWM, Keypad4x1.Pin2
  VCC: Part2.5V, LCM1602_IIC1.VCC, U1.VCC, ZS-042_RTC1.VCC, 125_kHz_RFID_module1.Vdd
  N9: Part2.D2_PWM, Keypad4x1.Pin8
  N10: Part2.D3_PWM, Keypad4x1.Pin7
  N11: Part2.D4_PWM, Keypad4x1.Pin6
  N12: Part2.D5_PWM, Keypad4x1.Pin5
  N13: Part2.D6_PWM, Keypad4x1.Pin4
  N14: Part2.D7_PWM, Keypad4x1.Pin3
  VSS: LCM1602_IIC1.VSS, LCD1.VSS
  VDD: LCM1602_IIC1.VDD, LCD1.VDD
  N15: LCM1602_IIC1.V0, LCD1.V0
  N16: LCM1602_IIC1.RS, LCD1.RS
  N17: LCM1602_IIC1.RW, LCD1.R/W
  N18: LCM1602_IIC1.E, LCD1.E
  N19: LCM1602_IIC1.D0, LCD1.DB0
  N20: LCM1602_IIC1.D1, LCD1.DB1
  N21: LCM1602_IIC1.D2, LCD1.DB2
  N22: LCM1602_IIC1.D3, LCD1.DB3
  N23: LCM1602_IIC1.D4, LCD1.DB4
  N24: LCM1602_IIC1.D5, LCD1.DB5
  N25: LCM1602_IIC1.D6, LCD1.DB6
  N26: LCM1602_IIC1.D7, LCD1.DB7
  N27: LCM1602_IIC1.A, LCD1.LED+
  N28: LCM1602_IIC1.K, LCD1.LED-
  N29: Part4.ANT1, 125_kHz_RFID_module1.ANT1
  N30: Part4.ANT2, 125_kHz_RFID_module1.ANT2

notes:
  Stop
  Start

custom parts:
  LCM1602 IIC: I2C-Module to use a 1602 or 2004 LCD on with the wire.h libory Serial LCD Modul
  Keypad Membran 4x4: Membrane Keypad 4x4 Matrix
  2-Channel 5v Relay Shield: 2 Channel 5v Relay Shield w. 2x SPD-06VDC-SD-C
  RDM6300-ANT: Antenna
  RDM6300: 125 kHz RFID module (serial interface)
